// Digital circuit 4x6bit Register Set.dig as structural Verilog
module _4x6bit_Register_Set (
  input  CLK,
  input  [5:0] WRD_5_0,
  input  REG_EN,
  input  [1:0] WR_1_0,
  input  [1:0] Ra_1_0,
  input  [1:0] Rb_1_0,
  output [5:0] A_5_0,
  output [5:0] B_5_0
);

  wire A0, A1, A2, A3, and_1_out, and_2_out, and_3_out, and_4_out;
  wire [5:0] R0, R1, R2, R3;

  and and_1 (and_1_out, A0, REG_EN);
  and and_2 (and_2_out, A1, REG_EN);
  and and_3 (and_3_out, A2, REG_EN);
  and and_4 (and_4_out, A3, REG_EN);
  Decoder #(.Selector_Bits(2)) decoder_1 (.sel(WR_1_0), .out_0(A0), .out_1(A1), .out_2(A2), .out_3(A3));
  _1x6bit_Register _1x6bit_register_1 (.Din_5_0(WRD_5_0), .Sel(and_1_out), .CLK(CLK), .Dout_5_0(R0));
  _1x6bit_Register _1x6bit_register_2 (.Din_5_0(WRD_5_0), .Sel(and_2_out), .CLK(CLK), .Dout_5_0(R1));
  _1x6bit_Register _1x6bit_register_3 (.Din_5_0(WRD_5_0), .Sel(and_3_out), .CLK(CLK), .Dout_5_0(R2));
  _1x6bit_Register _1x6bit_register_4 (.Din_5_0(WRD_5_0), .Sel(and_4_out), .CLK(CLK), .Dout_5_0(R3));
  Multiplexer #(.Bits(6), .Selector_Bits(2)) multiplexer_1 (
    .sel(Ra_1_0), .in_0(R0), .in_1(R1), .in_2(R2), .in_3(R3), .out(A_5_0));
  Multiplexer #(.Selector_Bits(2), .Bits(6)) multiplexer_2 (
    .sel(Rb_1_0), .in_0(R0), .in_1(R1), .in_2(R2), .in_3(R3), .out(B_5_0));
endmodule
