// Digital circuit 6bit CPU.dig as structural Verilog
module _6bit_CPU (
  input  [2:0] RA2_2_0,
  input  [2:0] WR_2_0,
  input  [17:0] WRD_17_0,
  input  WE,
  input  CLK,
  input  PC_EN,
  input  ZF,
  input  SF,
  output [17:0] RD2_17_0,
  output [5:0] R_5_0
);

  wire CPU_CLK, Imm_Sel, JMP_Sel, WE_t;
  wire [0:0] R2;
  wire [1:0] Op;
  wire [2:0] _3bit_pc_adder_1_o_2_0, _3bit_program_counter_1_o_2_0, JMP_Label, multiplexer_1_out;
  wire [3:0] Opcode;
  wire [5:0] _4x6bit_register_set_1_a_5_0, _4x6bit_register_set_1_b_5_0, multiplexer_2_out;
  wire [9:0] Don_t_Care;

  Multiplexer #(.Bits(3)) multiplexer_1 (
    .sel(JMP_Sel), .in_0(_3bit_pc_adder_1_o_2_0), .in_1(JMP_Label), .out(multiplexer_1_out));
  _3bit_Program_Counter _3bit_program_counter_1 (
    .I_2_0(multiplexer_1_out), .CLK(CPU_CLK), .O_2_0(_3bit_program_counter_1_o_2_0));
  _3bit_PC_Adder _3bit_pc_adder_1 (.I_2_0(_3bit_program_counter_1_o_2_0), .O_2_0(_3bit_pc_adder_1_o_2_0));
  and and_1 (CPU_CLK, CLK, PC_EN);
  _8x18_SRAM _8x18_sram_1 (
    .RA1_2_0(_3bit_program_counter_1_o_2_0), .RA2_2_0(RA2_2_0), .WR_2_0(WR_2_0), .WRD_17_0(WRD_17_0),
    .WE(WE), .CLK(CLK), .RD1_17_0({Opcode, JMP_Label, R2[0], Don_t_Care}), .RD2_17_0(RD2_17_0));
  Control_Unit control_unit_1 (
    .Opcode_3_0(Opcode), .Op_1_0(Op), .WE(WE_t), .Imm_Sel(Imm_Sel), .JMP_Sel(JMP_Sel), .ZF(ZF), .SF(SF));
  _4x6bit_Register_Set _4x6bit_register_set_1 (
    .WR_1_0(JMP_Label[2:1]), .CLK(CPU_CLK), .WRD_5_0(R_5_0), .REG_EN(WE_t), .Ra_1_0(JMP_Label[2:1]),
    .Rb_1_0({JMP_Label[0], R2[0]}), .A_5_0(_4x6bit_register_set_1_a_5_0), .B_5_0(_4x6bit_register_set_1_b_5_0));
  _6_bit_ALU _6_bit_alu_1 (.A_5_0(_4x6bit_register_set_1_a_5_0), .B_5_0(multiplexer_2_out), .Op_1_0(Op), .R_5_0(R_5_0));
  Multiplexer #(.Bits(6)) multiplexer_2 (
    .sel(Imm_Sel), .in_0(_4x6bit_register_set_1_b_5_0), .in_1({JMP_Label[0], R2[0], Don_t_Care[9:6]}),
    .out(multiplexer_2_out));

  // Other names for the same wires on the sheet: R2[1] = JMP_Label[0]; R1[1:0] = JMP_Label[2:1]; RD2[17:0] = RD2_17_0

  // Notes on the sheet:
  //   6-bit CPU:
  //   ======================================================
  //   Register Mode (00) = 2 Bit (Type of OP) + 2 Bit (Operation) + 2 Bit (Reg 1) + 2 Bit (Reg 2) + 10 Bit unused
  //   Immediate Mode (01) = 2 Bit (Type of OP) + 2 Bit (Operation) + 2 Bit (Reg 1) + 6-bit data + 6 Bit unused
  //   Branching Mode (10) = 2 Bit (Type of OP) + 2 Bit (Operation) + 3 Bit JMP Label + 11 Bit Unused
  //   OP Codes:
  //   ADD = 00
  //   XOR = 01
  //   SHR = 10
  //   JMP = 10 00
  //   JE = 10 01
  //   ADD R1, R1 = 000001010000000000
  //   XOR R1, 1 = 010101000001000000
  //   JMP 1 = 100000100000000000
endmodule
