// Digital circuit Control Unit.dig as structural Verilog
module Control_Unit (
  input  [3:0] Opcode_3_0,
  input  ZF,
  input  SF,
  output [1:0] Op_1_0,
  output Imm_Sel,
  output WE,
  output JMP_Sel
);

  wire and_1_out, and_4_out, and_5_out, JMP, not_1_out, not_2_out, not_3_out, or_1_out;

  and and_1 (and_1_out, ~Opcode_3_0[2], ~Opcode_3_0[3]);  // And
  and and_2 (Imm_Sel, Opcode_3_0[2], ~Opcode_3_0[3]);  // And
  and and_3 (JMP, ~Opcode_3_0[2], Opcode_3_0[3]);  // And
  or or_1 (or_1_out, and_1_out, Imm_Sel);
  not not_1 (not_1_out, SF);
  and and_4 (and_4_out, JMP, ~Opcode_3_0[0], ~Opcode_3_0[1]);  // And
  not not_2 (not_2_out, Opcode_3_0[1]);
  and and_5 (and_5_out, JMP, Opcode_3_0[0], not_2_out, ZF, not_1_out);
  not not_3 (not_3_out, JMP);
  and and_6 (WE, not_3_out, or_1_out);
  or or_2 (JMP_Sel, and_4_out, and_5_out);

  assign Op_1_0 = Opcode_3_0[1:0];

  // Notes on the sheet:
  //   For JE, CF is Don't Care
endmodule
