// Digital circuit 1x6bit Register.dig as structural Verilog
module _1x6bit_Register (
  input  [5:0] Din_5_0,
  input  CLK,
  input  Sel,
  output [5:0] Dout_5_0
);

  _1bit_Register _1bit_register_1 (.Din(Din_5_0[0]), .Sel(Sel), .CLK(CLK), .Dout(Dout_5_0[0]));
  _1bit_Register _1bit_register_2 (.Din(Din_5_0[1]), .Sel(Sel), .CLK(CLK), .Dout(Dout_5_0[1]));
  _1bit_Register _1bit_register_3 (.Din(Din_5_0[2]), .Sel(Sel), .CLK(CLK), .Dout(Dout_5_0[2]));
  _1bit_Register _1bit_register_4 (.Din(Din_5_0[3]), .Sel(Sel), .CLK(CLK), .Dout(Dout_5_0[3]));
  _1bit_Register _1bit_register_5 (.Din(Din_5_0[4]), .Sel(Sel), .CLK(CLK), .Dout(Dout_5_0[4]));
  _1bit_Register _1bit_register_6 (.Din(Din_5_0[5]), .Sel(Sel), .CLK(CLK), .Dout(Dout_5_0[5]));
endmodule
