// Digital circuit 6 bit ALU.dig as structural Verilog
module _6_bit_ALU (
  input  [5:0] A_5_0,
  input  [5:0] B_5_0,
  input  [1:0] Op_1_0,
  output [5:0] R_5_0
);

  wire [5:0] _6_bit_right_shifter_1_r_5_0, _6bit_adder_1_r_5_0, _6bit_xor_1_r_5_0;

  _6bit_Adder _6bit_adder_1 (.A_5_0(A_5_0), .B_5_0(B_5_0), .R_5_0(_6bit_adder_1_r_5_0));  // open: Cout
  _6bit_XOR _6bit_xor_1 (.A_5_0(A_5_0), .B_5_0(B_5_0), .R_5_0(_6bit_xor_1_r_5_0));
  _6_bit_Right_Shifter _6_bit_right_shifter_1 (.A_5_0(A_5_0), .B_5_0(B_5_0), .R_5_0(_6_bit_right_shifter_1_r_5_0));
  Multiplexer #(.Selector_Bits(2), .Bits(6)) multiplexer_1 (
    .sel(Op_1_0), .in_0(_6bit_adder_1_r_5_0), .in_1(_6bit_xor_1_r_5_0), .in_2(_6_bit_right_shifter_1_r_5_0),
    .in_3({6{1'b0}}), .out(R_5_0));
endmodule
