// Digital circuit 6bit XOR.dig as structural Verilog
module _6bit_XOR (
  input  [5:0] B_5_0,
  input  [5:0] A_5_0,
  output [5:0] R_5_0
);

  xor xor_1 (R_5_0[0], A_5_0[0], B_5_0[0]);
  xor xor_2 (R_5_0[1], A_5_0[1], B_5_0[1]);
  xor xor_3 (R_5_0[2], A_5_0[2], B_5_0[2]);
  xor xor_4 (R_5_0[3], A_5_0[3], B_5_0[3]);
  xor xor_5 (R_5_0[4], A_5_0[4], B_5_0[4]);
  xor xor_6 (R_5_0[5], A_5_0[5], B_5_0[5]);
endmodule
